# Fritzing sketch Engr132-PD1-Circuit-Design (saved by Fritzing 1.0.6)
breadboards: 1

parts:
  Part1 = Arduino Uno (Rev3) - ICSP
  J1 = Basic Servo
  SW-1 = Vibration sensor module
  LED1 = smd LED [color="Red (633nm)" package="1206 [SMD]"]
  LED2 = smd LED [color="Green (560nm)" package="1206 [SMD]"]
  J2 = Piezo Speaker
  R1 = Resistor [tolerance=±5% power=0.25W resistance=220 package=THT]
  R2 = Resistor [tolerance=±5% power=0.25W resistance=220 package=THT]
  R3 = Rotary Potentiometer (Small) [maximum_resistance=10kΩ knob_status=50% power=0.5W package=THT]
  LCD1 = LCD screen
  S1 = Pushbutton [package="[SMD]"]

nets:
  N1: Part1.A0, SW-1.Digital_output
  VCC: Part1.5V, J1.vcc, SW-1.vcc, R3.leg2, LCD1.VDD
  GND: Part1.GND, J1.gnd, SW-1.Ground, J2.pin1, R1.Pin_1, R2.Pin_1, R3.leg1, LCD1.VSS, S1.Pin_1, S1.Pin_2
  N2: Part1.D8, LED2.cathode
  N3: Part1.D9_PWM, LED1.cathode
  N4: Part1.D10_PWM/SS, J2.pin2
  N5: Part1.D11_PWM/MOSI, J1.pulse
  N6: Part1.D12/MISO, LCD1.E
  N7: Part1.D13/SCK, LCD1.RS
  N8: Part1.D2, S1.Pin_3, S1.Pin_4
  N9: Part1.D3_PWM, LCD1.DB7
  N10: Part1.D4, LCD1.DB6
  N11: Part1.D5_PWM, LCD1.DB5
  N12: Part1.D6_PWM, LCD1.DB4
  N13: LED1.anode, R1.Pin_0
  N14: LED2.anode, R2.Pin_0
  N15: R3.wiper, LCD1.V0

custom parts:
  Vibration sensor module: Single-roller type full induction trigger switch. When no vibration or tilt, the product is ON conduction state, and in the steady state, when a vibration or tilt, the switch will be rendered instantly disconnect the conductive resistance increases, generating a current pulse signal, thereby triggering circuit. The default state of the swith is close Digital output Supply voltage:3.3V-5V On-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
